# Fritzing sketch Lab Project Security Systems (saved by Fritzing 0.9.3b)
breadboards: 1

parts:
  Arduino_Uno = Arduino Uno (Rev3)
  R1 = Resistor [tolerance=±5% resistance=220 package=THT]
  LED1 = LED - 5mm [color="Red (633nm)" package="5 mm [THT]"]
  R2 = Resistor [tolerance=±5% resistance=220 package=THT]
  Keypad4x1 = Keypad Membran 4x4
  LCD_with_i2c = LCD1602-I2C
  Relay = KY-019 5V Relay Module [package="Breakout board"]
  S2 = Momentary Switch [package=ksa_sealed_tac_switch]
  S1 = Momentary Switch [package=ksa_sealed_tac_switch]
  R4 = Resistor [tolerance=±5% resistance=220 package=THT]
  L1 = Solenoid

nets:
  N1: Arduino_Uno.A4/SDA, LCD_with_i2c.SDA
  N2: Arduino_Uno.A5/SCL, LCD_with_i2c.SCL
  N3: Arduino_Uno.D8, Keypad4x1.Pin4
  N4: Arduino_Uno.D9_PWM, Keypad4x1.Pin3
  N5: Arduino_Uno.D10_PWM/SS, Keypad4x1.Pin2
  N6: Arduino_Uno.D11_PWM/MOSI, Keypad4x1.Pin1
  N7: Arduino_Uno.D13/SCK, Relay.S
  GND: Arduino_Uno.GND, R1.Pin_0, R2.Pin_1, LCD_with_i2c.GND, Relay.-
  N8: Arduino_Uno.D0/RX, S2.3, R4.Pin_1
  N9: Arduino_Uno.D2, LED1.cathode
  N10: Arduino_Uno.D3_PWM, R1.Pin_1, S1.3
  N11: Arduino_Uno.D4, Keypad4x1.Pin8
  N12: Arduino_Uno.D5_PWM, Keypad4x1.Pin7
  N13: Arduino_Uno.D6_PWM, Keypad4x1.Pin6
  N14: Arduino_Uno.D7, Keypad4x1.Pin5
  5V: Arduino_Uno.5V, LCD_with_i2c.VCC, Relay.+, S2.1, S1.1, R4.Pin_0
  N15: LED1.anode, R2.Pin_0
  N16: Relay.NO, L1.pin2

custom parts:
  Keypad Membran 4x4: Membrane Keypad 4x4 Matrix
  LCD1602-I2C: A standard character display, usually with 2x16 characters. Comes in many colors with LCM1602 IIC attached.
  KY-019 5V Relay Module: KY-019 5V Relay module, used to control AC circuits. (Special thanks to vanepp for fixing the PCB holes and other errors)
