# Fritzing sketch Security System (saved by Fritzing 0.9.3b)
breadboards: 1

parts:
  元件1 = Arduino Uno (Rev3)
  Keypad4x1 = Keypad Membran 4x4
  元件2 = LCD1602-I2C
  SP1 = SPEAKER [package=pcb_mount_speaker]
  Mod2 = laser receiver [package=THT]
  Mod3 = KY-008 Laser Transmitter Module [package="Breakout board"]
  R1 = Resistor [tolerance=±5% resistance=220 package=THT]

nets:
  N1: 元件1.A4/SDA, 元件2.SDA
  N2: 元件1.A5/SCL, 元件2.SCL
  N3: 元件1.D8, Keypad4x1.Pin4
  N4: 元件1.D9_PWM, Keypad4x1.Pin3
  N5: 元件1.D10_PWM/SS, Keypad4x1.Pin2
  N6: 元件1.D11_PWM/MOSI, Keypad4x1.Pin1
  N7: 元件1.D12/MISO, Mod3.S
  GND: 元件1.GND, 元件2.GND, Mod2.pin1, Mod3.-, R1.Pin_0
  N8: 元件1.D2, Mod2.pin2
  N9: 元件1.D3_PWM, SP1.-
  N10: 元件1.D4, Keypad4x1.Pin8
  N11: 元件1.D5_PWM, Keypad4x1.Pin7
  N12: 元件1.D6_PWM, Keypad4x1.Pin6
  N13: 元件1.D7, Keypad4x1.Pin5
  5V: 元件1.5V, 元件2.VCC, Mod2.pin3, Mod3.NC
  N14: SP1.+, R1.Pin_1

custom parts:
  Keypad Membran 4x4: Membrane Keypad 4x4 Matrix
  LCD1602-I2C: A standard character display, usually with 2x16 characters. Comes in many colors with LCM1602 IIC attached.
  laser receiver: Generic non modulated laser receiver module.
  KY-008 Laser Transmitter Module: KY-008 Laser Transmitter Module, emits a dot shaped red laser beam.
